# Fritzing sketch schematic (saved by Fritzing 0.9.3b)
breadboards: 2

parts:
  U1 = ESP8266 WiFi Module [part_number=ESP8266]
  Q1 = MOSFET-NCHANNEL [package=to-92]
  C1 = Tantalum Capacitor [capacitance="1 μF" package="C 6032 [SMD, tantalum]"]
  C2 = Tantalum Capacitor [capacitance="1 μF" package="C 6032 [SMD, tantalum]"]
  U3 = 74HC595 [package="DIP16 [THT]"]
  C3 = Electrolytic Capacitor [capacitance=100μF package="0807 [SMD, electrolytic]"]
  C5 = Ceramic Capacitor [capacitance=10nF package="0805 [SMD, multilayer]"]
  R1 = Resistor [tolerance=±5% resistance=10k package="2512 [SMD]"]
  R2 = Resistor [tolerance=±5% resistance=10k package="2512 [SMD]"]
  R3 = Resistor [tolerance=±5% resistance=10k package="2512 [SMD]"]
  S1_(S/W_Button) = SWITCH-MOMENTARY-2 [package=tactile-pth]
  S2_(H/W_Reset) = SWITCH-MOMENTARY-2 [package=tactile-pth]
  LM1117t = Voltage Regulator - 3.3V [package="TO220 [THT]"]
  USB_supplies_VBUS_and_GND = USB Connectors [package=usb-minib-nostop]
  LED1 = LED - 3mm [color="Blue (430nm)" package="3 mm [THT]"]
  LED2 = LED - 3mm [color="Blue (470nm)" package="3 mm [THT]"]
  LED3 = LED - 3mm [color="Blue (470nm)" package="3 mm [THT]"]
  LED4 = LED - 3mm [color="Blue (470nm)" package="3 mm [THT]"]
  LED = LED - 3mm [color="Blue (470nm)" package="3 mm [THT]"]
  LED6 = LED - 3mm [color="Blue (470nm)" package="3 mm [THT]"]
  LED7 = LED - 3mm [color="Blue (470nm)" package="3 mm [THT]"]
  LED8 = LED - 3mm [color="Blue (470nm)" package="3 mm [THT]"]

nets:
  VCC: U1.VCC, C1.+, U3.MR, U3.VCC, C3.+, C5.1, R2.Pin_1, R3.Pin_0, LM1117t.output_voltage
  N1: U1.GPIO_2, R3.Pin_1
  N2: U1.CH_PD, R2.Pin_0, S2_(H/W_Reset).2
  GND: U1.GND, Q1.S, C1.-, C2.-, U3.GND, U3.OE, C3.-, C5.0, R1.Pin_0, S1_(S/W_Button).2, S2_(H/W_Reset).1, LM1117t.GND, USB_supplies_VBUS_and_GND.GND
  N3: U1.GPIO_15, U3.ST_CP, R1.Pin_1
  N4: U1.GPIO_4, Q1.G
  N5: U1.GPIO_5, S1_(S/W_Button).1
  N6: U1.GPIO_14, U3.SH_CP
  N7: U1.GPIO_13, U3.DS
  N8: Q1.D, LED1.cathode, LED2.cathode, LED3.cathode, LED4.cathode, LED.cathode, LED6.cathode, LED7.cathode, LED8.cathode
  N9: C2.+, LM1117t.input_voltage, USB_supplies_VBUS_and_GND.VBUS
  N10: U3.Q1, LED2.anode
  N11: U3.Q2, LED3.anode
  N12: U3.Q3, LED4.anode
  N13: U3.Q4, LED.anode
  N14: U3.Q5, LED6.anode
  N15: U3.Q6, LED7.anode
  N16: U3.Q7, LED8.anode
  N17: U3.Q0, LED1.anode
